// Logisim project cpu.circ as structural Verilog
module half_adder (
  input  A,
  input  B,
  output SUM___A_xor_B,
  output CARRY___A_and_B
);

  xor xor_1 (SUM___A_xor_B, B, A);
  and and_1 (CARRY___A_and_B, A, B);

  // Notes on the sheet:
  //   A: pull=down
  //   B: pull=down
  //   CARRY___A_and_B: pull=down
  //   SUM___A_xor_B: pull=down
endmodule

module full_adder (
  input  in_1,
  input  in_2,
  input  in_3,
  output sum,
  output carry_out
);

  wire A_xor_B, and_1_out, and_2_out;

  xor xor_1 (A_xor_B, in_1, in_2);
  and and_1 (and_1_out, in_3, A_xor_B);
  and and_2 (and_2_out, in_1, in_2);
  xor xor_2 (sum, A_xor_B, in_3);
  or or_1 (carry_out, and_1_out, and_2_out);

  // Other names for the same wires on the sheet: A = in_1; B = in_2; carry_in = in_3

  // Notes on the sheet:
  //   sum: pull=down
  //   carry_out: pull=down
endmodule

module _8_bit_full_adder (
  input  [7:0] A,
  input  [7:0] B,
  input  in_3,
  output [7:0] sum,
  output carry_out
);

  wire full_adder_1_carry_out, full_adder_2_carry_out, full_adder_3_carry_out, full_adder_4_carry_out,
       full_adder_5_carry_out, full_adder_6_carry_out, full_adder_7_carry_out;

  full_adder full_adder_1 (.in_1(A[0]), .in_2(B[0]), .in_3(in_3), .sum(sum[0]), .carry_out(full_adder_1_carry_out));
  full_adder full_adder_2 (
    .in_1(A[1]), .in_2(B[1]), .in_3(full_adder_1_carry_out), .sum(sum[1]), .carry_out(full_adder_2_carry_out));
  full_adder full_adder_3 (
    .in_1(A[2]), .in_2(B[2]), .in_3(full_adder_2_carry_out), .sum(sum[2]), .carry_out(full_adder_3_carry_out));
  full_adder full_adder_4 (
    .in_1(A[3]), .in_2(B[3]), .in_3(full_adder_3_carry_out), .sum(sum[3]), .carry_out(full_adder_4_carry_out));
  full_adder full_adder_5 (
    .in_1(A[4]), .in_2(B[4]), .in_3(full_adder_4_carry_out), .sum(sum[4]), .carry_out(full_adder_5_carry_out));
  full_adder full_adder_6 (
    .in_1(A[5]), .in_2(B[5]), .in_3(full_adder_5_carry_out), .sum(sum[5]), .carry_out(full_adder_6_carry_out));
  full_adder full_adder_7 (
    .in_1(A[6]), .in_2(B[6]), .in_3(full_adder_6_carry_out), .sum(sum[6]), .carry_out(full_adder_7_carry_out));
  full_adder full_adder_8 (
    .in_1(A[7]), .in_2(B[7]), .in_3(full_adder_7_carry_out), .sum(sum[7]), .carry_out(carry_out));

  // Other names for the same wires on the sheet: carry_in = in_3

  // Notes on the sheet:
  //   sum: pull=down
  //   carry_out: pull=down
endmodule

module _16_bit_full_adder (
  input  [15:0] A,
  input  [15:0] B,
  input  in_3,
  output [15:0] \output ,
  output carry_out
);

  wire full_adder_1_carry_out, full_adder_2_carry_out, full_adder_3_carry_out, full_adder_4_carry_out,
       full_adder_5_carry_out, full_adder_6_carry_out, full_adder_7_carry_out, full_adder_8_carry_out,
       full_adder_9_carry_out, full_adder_10_carry_out, full_adder_11_carry_out, full_adder_12_carry_out,
       full_adder_13_carry_out, full_adder_14_carry_out, full_adder_15_carry_out;

  full_adder full_adder_1 (
    .in_1(A[0]), .in_2(B[0]), .in_3(in_3), .sum(\output [0]), .carry_out(full_adder_1_carry_out));
  full_adder full_adder_2 (
    .in_1(A[1]), .in_2(B[1]), .in_3(full_adder_1_carry_out), .sum(\output [1]),
    .carry_out(full_adder_2_carry_out));
  full_adder full_adder_3 (
    .in_1(A[2]), .in_2(B[2]), .in_3(full_adder_2_carry_out), .sum(\output [2]),
    .carry_out(full_adder_3_carry_out));
  full_adder full_adder_4 (
    .in_1(A[3]), .in_2(B[3]), .in_3(full_adder_3_carry_out), .sum(\output [3]),
    .carry_out(full_adder_4_carry_out));
  full_adder full_adder_5 (
    .in_1(A[4]), .in_2(B[4]), .in_3(full_adder_4_carry_out), .sum(\output [4]),
    .carry_out(full_adder_5_carry_out));
  full_adder full_adder_6 (
    .in_1(A[5]), .in_2(B[5]), .in_3(full_adder_5_carry_out), .sum(\output [5]),
    .carry_out(full_adder_6_carry_out));
  full_adder full_adder_7 (
    .in_1(A[6]), .in_2(B[6]), .in_3(full_adder_6_carry_out), .sum(\output [6]),
    .carry_out(full_adder_7_carry_out));
  full_adder full_adder_8 (
    .in_1(A[7]), .in_2(B[7]), .in_3(full_adder_7_carry_out), .sum(\output [7]),
    .carry_out(full_adder_8_carry_out));
  full_adder full_adder_9 (
    .in_1(A[8]), .in_2(B[8]), .in_3(full_adder_8_carry_out), .sum(\output [8]),
    .carry_out(full_adder_9_carry_out));
  full_adder full_adder_10 (
    .in_1(A[9]), .in_2(B[9]), .in_3(full_adder_9_carry_out), .sum(\output [9]),
    .carry_out(full_adder_10_carry_out));
  full_adder full_adder_11 (
    .in_1(A[10]), .in_2(B[10]), .in_3(full_adder_10_carry_out), .sum(\output [10]),
    .carry_out(full_adder_11_carry_out));
  full_adder full_adder_12 (
    .in_1(A[11]), .in_2(B[11]), .in_3(full_adder_11_carry_out), .sum(\output [11]),
    .carry_out(full_adder_12_carry_out));
  full_adder full_adder_13 (
    .in_1(A[12]), .in_2(B[12]), .in_3(full_adder_12_carry_out), .sum(\output [12]),
    .carry_out(full_adder_13_carry_out));
  full_adder full_adder_14 (
    .in_1(A[13]), .in_2(B[13]), .in_3(full_adder_13_carry_out), .sum(\output [13]),
    .carry_out(full_adder_14_carry_out));
  full_adder full_adder_15 (
    .in_1(A[14]), .in_2(B[14]), .in_3(full_adder_14_carry_out), .sum(\output [14]),
    .carry_out(full_adder_15_carry_out));
  full_adder full_adder_16 (
    .in_1(A[15]), .in_2(B[15]), .in_3(full_adder_15_carry_out), .sum(\output [15]), .carry_out(carry_out));

  // Other names for the same wires on the sheet: carry_in = in_3

  // Notes on the sheet:
  //   A: pull=down
  //   carry_out: pull=down
  //   output: pull=down
  //   B: pull=down
endmodule
